# Fritzing sketch parksensor (saved by Fritzing 0.9.6b)
circuit board: 8.46667cm x 5.64444cm
breadboards: 1

parts:
  Arduino1 = Arduino Mini (Rev5)
  part = HC-SR04 Ultrasonic Distance Sensor
  HC-SR04_Sensor_3 = HC-SR04 Ultrasonic Distance Sensor
  part_2 = HC-SR04 Ultrasonic Distance Sensor
  HC-SR04_Sensor_5 = HC-SR04 Ultrasonic Distance Sensor

nets:
  N1: Arduino1.D4, part_2.ECHO
  N2: Arduino1.D6_PWM, HC-SR04_Sensor_5.ECHO
  N3: Arduino1.D7, HC-SR04_Sensor_5.VCC
  N4: Arduino1.D8, part.ECHO
  N5: Arduino1.D9_PWM, part.VCC
  N6: Arduino1.A1, HC-SR04_Sensor_3.ECHO
  N7: Arduino1.A0, HC-SR04_Sensor_3.VCC
  GND: part.GND, HC-SR04_Sensor_3.GND, part_2.GND, HC-SR04_Sensor_5.GND
